# Fritzing sketch Analog Joystick Module (saved by Fritzing 0.9.10b)
breadboards: 1

parts:
  Part1 = Arduino Mega 2560 (Rev3)
  Part2 = Thumb Joystick
  LCD1 = LCD screen
  U1 = POT [knob_status=50% power=0.5W package=pot_alpha_rv16af-20]

nets:
  N1: Part1.A0, Part2.HORZ
  N2: Part1.A1, Part2.VERT
  N3: Part1.A2, Part2.SEL
  5V: Part1.5V, Part2.VCC
  GND: Part1.GND, Part2.GND
  N4: Part1.D4_PWM, LCD1.DB0
  N5: LCD1.R/W, LCD1.DB3
  N6: LCD1.DB1, LCD1.DB6
  N7: LCD1.DB4, U1.E
