# Fritzing sketch Distance Sensor (saved by Fritzing 0.9.10b)
breadboards: 3

parts:
  Part1 = Arduino Mega 2560 (Rev3)
  LCD1 = LCD screen
  LCD2 = LCD screen
  S1 = Pushbutton [package="[THT]"]
  S2 = Pushbutton [package="[THT]"]
  HC-SR04_Sensor_1 = HC-SR04 Ultrasonic Distance Sensor
  RHT1 = Humidity and Temperature Sensor RHT03
  U1 = POT [knob_status=50% power=0.5W package=pot_mammoth]

nets:
  GND: Part1.GND, LCD1.VSS, LCD1.RS, LCD1.LED-, LCD2.VSS, LCD2.RS, LCD2.LED+, S1.Pin_3, S1.Pin_4, S2.Pin_3, S2.Pin_4, HC-SR04_Sensor_1.GND, U1.S
  N1: Part1.D13_PWM, HC-SR04_Sensor_1.ECHO
  N2: Part1.D12_PWM, HC-SR04_Sensor_1.TRIG
  N3: Part1.D11_PWM, LCD1.LED+, LCD2.DB7
  N4: Part1.D9_PWM, LCD1.E
  N5: Part1.D8_PWM, LCD1.V0
  N6: Part1.D3_PWM, RHT1.Data-signal
  N7: Part1.D4_PWM, LCD1.DB4
  N8: Part1.D5_PWM, LCD1.DB5
  N9: Part1.D6_PWM, LCD1.DB6
  N10: Part1.D7_PWM, LCD1.DB7
  VDD: Part1.5V, LCD1.VDD, LCD2.VDD, HC-SR04_Sensor_1.VCC
  N11: Part1.D23, LCD2.DB6
  N12: Part1.D25, LCD2.DB5
  N13: Part1.D27, LCD2.DB4
  N14: Part1.D29, LCD2.DB3
  N15: Part1.D31, LCD2.DB0
  N16: Part1.D33, LCD2.R/W
  N17: Part1.D35, S2.Pin_1, S2.Pin_2
  N18: Part1.D39, S1.Pin_1, S1.Pin_2
  N19: LCD1.R/W, LCD2.V0, U1.A
