# Fritzing sketch Motion Sensor (saved by Fritzing 0.9.10b)

parts:
  Part1 = HC-SR501 Body Sensor Module
  Part2 = Arduino Mega 2560 (Rev3)

nets:
  VCC: Part1.VCC, Part2.3V3
  N1: Part1.OUT, Part2.D7_PWM
  GND: Part1.GND, Part2.GND

custom parts:
  HC-SR501 Body Sensor Module: Pyroelectric Infrared PIR Motion Sensor Detector Module
