# Fritzing sketch Compliment Generator (saved by Fritzing 0.9.10b)
breadboards: 1

parts:
  LCD1 = LCD screen
  U1 = POT [knob_status=50% power=0.5W package=pot_mammoth]
  Part2 = Arduino Uno (Rev3)

nets:
  VSS: LCD1.VSS, LCD1.R/W, LCD1.LED-, U1.E, Part2.GND
  VDD: LCD1.VDD, Part2.5V
  N1: LCD1.V0, U1.A
  N2: LCD1.RS, Part2.D2
  N3: LCD1.E, Part2.D3_PWM
  N4: LCD1.DB4, Part2.D4
  N5: LCD1.DB5, Part2.D5_PWM
  N6: LCD1.DB6, Part2.D6_PWM
  N7: LCD1.DB7, Part2.D7
  N8: LCD1.LED+, Part2.D8
