# Fritzing sketch 4x4 keypad breadboard (saved by Fritzing 0.9.10b)
breadboards: 1

parts:
  R1 = BBC MicroBit
  J1 = female pin header, 8 pins [form="♀ (female)"]
  R2 = Resistor [tolerance=±5% resistance=220 power=0.25 package=THT]  # not connected
  R3 = Resistor [tolerance=±5% resistance=220 power=0.25 package=THT]
  R4 = Resistor [tolerance=±5% resistance=220 power=0.25 package=THT]
  R5 = Resistor [tolerance=±5% resistance=220 power=0.25 package=THT]
  R6 = Resistor [tolerance=±5% resistance=1k power=0.25 package=THT]
  R7 = Resistor [tolerance=±5% resistance=1k power=0.25 package=THT]
  R8 = Resistor [tolerance=±5% resistance=1k power=0.25 package=THT]
  R9 = Resistor [tolerance=±5% resistance=1k power=0.25 package=THT]
  Keypad4x1 = Keypad Membran 4x4
  R10 = Resistor [tolerance=±5% resistance=10k power=0.25 package=THT]

nets:
  N1: R1.GND, R10.Pin_1
  N2: R1.3v3, R9.Pin_0
  N3: R1.P1_ANALOG_IN, J1.pin5, R5.Pin_0, Keypad4x1.Pin5, R10.Pin_0
  N4: J1.pin1, R8.Pin_0, R9.Pin_1, Keypad4x1.Pin1
  N5: J1.pin2, R7.Pin_0, R8.Pin_1, Keypad4x1.Pin2
  N6: J1.pin3, R6.Pin_0, R7.Pin_1, Keypad4x1.Pin3
  N7: J1.pin4, R6.Pin_1, Keypad4x1.Pin4
  N8: J1.pin6, R4.Pin_0, R5.Pin_1, Keypad4x1.Pin6
  N9: J1.pin7, R3.Pin_0, R4.Pin_1, Keypad4x1.Pin7
  N10: J1.pin8, R3.Pin_1, Keypad4x1.Pin8

custom parts:
  BBC MicroBit: The BBC MICRO:BIT
  Keypad Membran 4x4: Membrane Keypad 4x4 Matrix
