# Fritzing sketch Membrane Switch Module (saved by Fritzing 0.9.10b)
breadboards: 1

parts:
  Part1 = Arduino Mega 2560 (Rev3)
  LCD1 = LCD screen
  U1 = POT [knob_status=50% power=0.5W package=pot_mammoth]
  Keypad4x1 = Keypad Membran 4x4

nets:
  GND: Part1.GND, LCD1.VSS, LCD1.LED-, U1.E
  N1: Part1.D10_PWM, LCD1.DB7
  N2: Part1.D9_PWM, LCD1.DB6
  N3: Part1.D8_PWM, LCD1.DB5
  N4: Part1.D7_PWM, LCD1.DB4
  N5: Part1.D39, Keypad4x1.Pin1
  N6: Part1.D41, Keypad4x1.Pin2
  N7: Part1.D43, Keypad4x1.Pin3
  N8: Part1.D45, Keypad4x1.Pin4
  N9: Part1.D47, Keypad4x1.Pin5
  N10: Part1.D49, Keypad4x1.Pin6
  N11: Part1.D51, Keypad4x1.Pin7
  N12: Part1.D53, Keypad4x1.Pin8
  N13: LCD1.VDD, LCD1.LED+
  N14: LCD1.V0, U1.A

custom parts:
  Keypad Membran 4x4: Membrane Keypad 4x4 Matrix
