# Fritzing sketch RC522 RFID Module (saved by Fritzing 0.9.10b)
breadboards: 1

parts:
  Part1 = Arduino Mega 2560 (Rev3)
  LCD1 = LCD screen
  U1 = POT [knob_status=50% power=0.5W package=pot_mammoth]
  Part2 = RFID-RC522-v2

nets:
  GND: Part1.GND, LCD1.VSS, LCD1.R/W, LCD1.LED-, U1.E, Part2.GND
  N1: Part1.D13_PWM, Part2.SCK
  N2: Part1.D12_PWM, Part2.MISO
  N3: Part1.D11_PWM, Part2.MOSI
  N4: Part1.D10_PWM, Part2.SDA
  N5: Part1.D9_PWM, Part2.RST
  N6: Part1.D8_PWM, LCD1.LED+
  3V3: Part1.3V3, Part2.3.3V
  N7: Part1.D2_PWM, LCD1.RS
  N8: Part1.D3_PWM, LCD1.E
  N9: Part1.D4_PWM, LCD1.DB4
  N10: Part1.D5_PWM, LCD1.DB5
  N11: Part1.D6_PWM, LCD1.DB6
  N12: Part1.D7_PWM, LCD1.DB7
  5V: Part1.5V, LCD1.VDD
  N13: LCD1.V0, U1.A

custom parts:
  RFID-RC522-v2: A simple China made RFID-RC522 Reader; do check the pin labels, as this is a MFRC522 based clone.
