# Fritzing sketch Real Time Clock Module (saved by Fritzing 0.9.10b)
breadboards: 1

parts:
  Part1 = Arduino Mega 2560 (Rev3)
  LCD1 = LCD screen
  U1 = POT [knob_status=50% power=0.5W package=pot_mammoth]
  Part2 = Real Time Clock Module - DS1307 RTC Breakout Board

nets:
  N1: Part1.D20/SDA, Part1.SDA, Part2.SDA
  N2: Part1.SCL, Part2.SCL
  GND: Part1.GND, LCD1.VSS, LCD1.R/W, LCD1.LED-, U1.E, Part2.GND
  N3: Part1.D8_PWM, LCD1.LED+
  5V: Part1.5V, LCD1.VDD, Part2.5V
  N4: Part1.D2_PWM, LCD1.RS
  N5: Part1.D3_PWM, LCD1.E
  N6: Part1.D4_PWM, LCD1.DB4
  N7: Part1.D5_PWM, LCD1.DB5
  N8: Part1.D6_PWM, LCD1.DB6
  N9: Part1.D7_PWM, LCD1.DB7
  N10: LCD1.V0, U1.A
