# Fritzing sketch Water Level Sensor (saved by Fritzing 0.9.10b)
breadboards: 1

parts:
  Part1 = Arduino Mega 2560 (Rev3)
  LCD1 = LCD screen
  U1 = POT [knob_status=50% power=0.5W package=pot_mammoth]
  Water_Level_Sensor1 = Water Level Sensor

nets:
  N1: Part1.A0, Water_Level_Sensor1.SIG
  GND: Part1.GND, LCD1.VSS, LCD1.R/W, LCD1.LED-, U1.E, Water_Level_Sensor1.GND
  N2: Part1.D8_PWM, LCD1.LED+
  5V: Part1.5V, LCD1.VDD, Water_Level_Sensor1.VCC
  N3: Part1.D2_PWM, LCD1.RS
  N4: Part1.D3_PWM, LCD1.E
  N5: Part1.D4_PWM, LCD1.DB4
  N6: Part1.D5_PWM, LCD1.DB5
  N7: Part1.D6_PWM, LCD1.DB6
  N8: Part1.D7_PWM, LCD1.DB7
  N9: LCD1.V0, U1.A

custom parts:
  Water Level Sensor: A water level sensor. This sensor operates at 3V to 5V. The Sig (signal) pin outputs an analogue signal that is in proportion to the amount of water in contact with the sensor.
